// Digital circuit CPU.dig as structural Verilog
module CPU (
  input  [7:0] Input,
  input  clk,
  output [7:0] Output
);

  wire and_1_out, and_2_out, and_3_out, and_4_out, and_5_out, and_6_out, and_7_out, and_8_out, and_9_out,
       and_10_out, and_11_out, and_12_out, and_13_out, and_14_out, and_15_out, and_16_out, and_17_out,
       and_18_out, and_19_out, and_20_out, and_21_out, and_22_out, and_23_out, and_24_out, and_25_out,
       and_26_out, and_27_out, and_28_out, and_29_out, and_30_out, and_31_out, and_32_out, and_33_out,
       and_34_out, and_35_out, and_36_out, and_37_out, button_1_out, Clk_t, comparator_1_eq, comparator_2_eq,
       delay_1_out, dipswitch_1_out, not_1_out, not_3_out, not_4_out, not_5_out, not_6_out, not_7_out,
       not_8_out, or_1_out, or_2_out, or_3_out, or_4_out, or_5_out, or_6_out, or_7_out, or_8_out, Proceed,
       rs_ff_1_q, rs_ff_2_q, rs_ff_3_q, rs_ff_4_nq, rs_ff_4_q, rs_ff_5_q, Send_out, xor_1_out;
  wire [7:0] Changer_out, Data_d, driver_1_out, not_2_out, rom_1_d;
  wire [15:0] Depth_out, Pointer_out, ProgAddr, register_1_q;
  wire [15:15] undriven;

  DipSwitch dipswitch_1 (.out(dipswitch_1_out));
  Button button_1 (.out(button_1_out));
  Multiplexer multiplexer_1 (.sel(dipswitch_1_out), .in_0(button_1_out), .in_1(clk), .out(Clk_t));
  ROM #(.AddrBits(16), .Bits(8)) rom_1 (.A(ProgAddr), .sel(1'b1), .D(rom_1_d));
  not not_1 (not_1_out, or_1_out);
  or or_1 (or_1_out, or_1_out, and_1_out);
  and and_1 (and_1_out, Clk_t, Proceed);
  assign not_2_out = ~rom_1_d;  // Not not_2, 8 bits wide
  or or_2 (or_2_out, rs_ff_3_q, not_1_out);
  RS_FF rs_ff_1 (.S(or_2_out), .C(and_1_out), .R(rs_ff_1_q), .Q(rs_ff_1_q));  // open: nQ
  LED led_1 (.in(rs_ff_1_q));
  and and_2 (and_2_out, rom_1_d[0], rom_1_d[1], not_2_out[2], rom_1_d[3]);
  and and_3 (and_3_out, rom_1_d[0], not_2_out[1], rom_1_d[2], rom_1_d[3]);
  and and_4 (and_4_out, not_2_out[4], rom_1_d[5], not_2_out[6], not_2_out[7]);
  and and_5 (and_5_out, not_2_out[0], not_2_out[1], rom_1_d[2], rom_1_d[3]);
  and and_6 (and_6_out, not_2_out[0], rom_1_d[1], rom_1_d[2], rom_1_d[3]);
  and and_7 (and_7_out, rom_1_d[4], rom_1_d[5], not_2_out[6], not_2_out[7]);
  and and_8 (and_8_out, rom_1_d[4], not_2_out[5], rom_1_d[6], not_2_out[7]);
  RS_FF rs_ff_2 (.S(rs_ff_1_q), .C(and_1_out), .R(rs_ff_2_q), .Q(rs_ff_2_q));  // open: nQ
  LED led_2 (.in(rs_ff_2_q));
  and and_9 (and_9_out, and_2_out, and_4_out);
  and and_10 (and_10_out, and_3_out, and_4_out);
  and and_11 (and_11_out, and_5_out, and_4_out);
  and and_12 (and_12_out, and_6_out, and_4_out);
  and and_13 (and_13_out, and_5_out, and_7_out);
  and and_14 (and_14_out, and_6_out, and_7_out);
  and and_15 (and_15_out, and_2_out, and_8_out);
  and and_16 (and_16_out, and_3_out, and_8_out);
  RS_FF rs_ff_3 (.S(rs_ff_2_q), .C(and_1_out), .R(rs_ff_3_q), .Q(rs_ff_3_q));  // open: nQ
  LED led_3 (.in(rs_ff_3_q));
  LED led_4 (.in(and_9_out));
  LED led_5 (.in(and_10_out));
  LED led_6 (.in(and_11_out));
  LED led_7 (.in(and_12_out));
  LED led_8 (.in(and_13_out));
  LED led_9 (.in(and_14_out));
  and and_17 (and_17_out, rs_ff_1_q, rs_ff_4_nq);
  LED led_10 (.in(and_15_out));
  LED led_11 (.in(and_16_out));
  and and_18 (and_18_out, rs_ff_2_q, rs_ff_4_nq);
  and and_19 (and_19_out, and_18_out, and_10_out);
  or or_3 (or_3_out, and_9_out, and_10_out);
  and and_20 (and_20_out, and_18_out, and_11_out);
  and and_21 (and_21_out, and_17_out, and_12_out);
  and and_22 (and_22_out, and_17_out, and_13_out);
  and and_23 (and_23_out, and_17_out, and_14_out);
  and and_24 (and_24_out, rs_ff_3_q, rs_ff_4_nq);
  Comparator #(.Bits(8)) comparator_1 (.a(Data_d), .b({8{1'b0}}), .eq(comparator_1_eq));  // open: gt, lt
  and and_25 (and_25_out, and_17_out, or_3_out);
  and and_26 (and_26_out, and_18_out, or_3_out);
  and and_27 (and_27_out, and_8_out, rs_ff_1_q);
  and and_28 (and_28_out, comparator_1_eq, and_15_out);
  not not_3 (not_3_out, comparator_1_eq);
  or or_4 (or_4_out, and_26_out, and_20_out);
  or or_5 (or_5_out, and_25_out, and_21_out);
  or or_6 (or_6_out, and_28_out, and_29_out);
  and and_29 (and_29_out, not_3_out, and_16_out);
  xor xor_1 (xor_1_out, and_16_out, rs_ff_5_q);
  CounterPreset #(.Bits(16)) Depth (
    .en(and_27_out), .C(Clk_t), .dir(xor_1_out), .in({undriven[15], {15{1'b0}}}), .ld(1'b0), .clr(1'b0),
    .out(Depth_out));  // open: ovf
  and and_30 (and_30_out, rs_ff_2_q, and_32_out);
  and and_31 (and_31_out, rs_ff_1_q, and_16_out);
  and and_32 (and_32_out, comparator_2_eq, not_4_out);
  or or_7 (or_7_out, and_24_out, and_36_out);
  or or_8 (or_8_out, and_23_out, and_22_out);
  and and_33 (and_33_out, or_6_out, rs_ff_2_q);
  and and_34 (and_34_out, and_31_out, or_6_out);
  not not_4 (not_4_out, or_6_out);
  not not_5 (not_5_out, Clk_t);
  and and_35 (and_35_out, or_6_out, and_27_out);
  CounterPreset #(.Bits(16)) Counter (
    .en(or_7_out), .C(Clk_t), .dir(rs_ff_5_q), .in({16{1'b0}}), .ld(1'b0), .clr(1'b0), .out(ProgAddr));  // open: ovf
  not not_6 (not_6_out, Clk_t);
  CounterPreset #(.Bits(16)) Pointer (
    .en(or_8_out), .C(Clk_t), .dir(and_22_out), .in({16{1'b0}}), .ld(1'b0), .clr(1'b0), .out(Pointer_out));  // open: ovf
  not not_7 (not_7_out, Clk_t);
  Delay delay_1 (.in(and_20_out), .out(delay_1_out));
  not not_8 (not_8_out, delay_1_out);
  RS_FF rs_ff_4 (.S(and_33_out), .C(Clk_t), .R(and_30_out), .Q(rs_ff_4_q), .nQ(rs_ff_4_nq));
  RS_FF rs_ff_5 (.S(and_34_out), .C(not_6_out), .R(and_30_out), .Q(rs_ff_5_q));  // open: nQ
  Register #(.Bits(16)) register_1 (.D(Depth_out), .C(not_5_out), .en(and_35_out), .Q(register_1_q));
  // Probe on ProgAddr
  // Probe on Pointer_out
  RAMDualPort #(.AddrBits(16), .Bits(8)) Data (
    .A(Pointer_out), .Din(driver_1_out), .str(or_4_out), .C(Clk_t), .ld(1'b1), .D(Data_d));
  and and_36 (and_36_out, rs_ff_4_q, rs_ff_3_q);
  // Probe on register_1_q
  Comparator #(.Bits(16)) comparator_2 (.a(register_1_q), .b(Depth_out), .eq(comparator_2_eq));  // open: gt, lt
  // Probe on Depth_out
  and and_37 (and_37_out, and_20_out, not_8_out);
  // Probe on Data_d
  assign driver_1_out = or_5_out ? Data_d : 8'bz;  // Driver driver_1
  CounterPreset #(.Bits(8)) Changer (
    .en(1'b1), .C(not_7_out), .dir(and_19_out), .in(driver_1_out), .ld(and_25_out), .clr(1'b0),
    .out(Changer_out));  // open: ovf
  assign driver_1_out = and_26_out ? Changer_out : 8'bz;  // Driver driver_2
  assign driver_1_out = and_20_out ? Input : 8'bz;  // Driver driver_3
  RS_FF_AS rs_ff_as_1 (.S(and_37_out), .R(Send_out), .nQ(Proceed));  // open: Q
  Register #(.Bits(8)) register_2 (.D(driver_1_out), .C(Clk_t), .en(and_21_out), .Q(Output));
  Button Send (.out(Send_out));
  LED led_12 (.in(and_21_out));
  // Pins of 15 and 16 bits meet at {undriven[15], {15{1'b0}}}

  // Notes on the sheet:
  //   clk: Hz: 10
  //   + -
  //   , .
  //   < >
  //   [ ]
  //   rom_1 loads program.bf
  //   +
  //   -
  //   ,
  //   .
  //   <
  //   >
  //   [
  //   ]
  //   Counter_Inc
  //   Pointer_Inc
  //   Pointer_Dec
  //   Changer_Sub
  //   Changer_In
  //   Changer_Out
  //   Input_Out
  //   Input_Await
  //   Output_In
  //   Data_In
  //   Data_Out
  //   Should Trigger
  //   Target Depth
  //   Current Depth
  //   Seek
  //   Dir
endmodule
